# Fritzing sketch servo (saved by Fritzing 0.7.10b)

parts:
  U1 = Voltage Regulator - 5V [package="DPak [SMD]"]
  VCC1 = Battery block 9V
  U2 = Voltage Regulator - 5V [package="TO220 [THT]"]
  J1 = Basic Servo
  Arduino1 = Arduino

nets:
  N1: U1.input_voltage, VCC1.+
  N2: U1.GND, VCC1.-
  N3: U1.output_voltage, U2.input_voltage
  GND: U2.GND, J1.gnd
  N4: U2.output_voltage, J1.vcc
  N5: J1.pulse, Arduino1.D9

notes:
  12v 10A power supply
  7809 voltage regulator
  7805 voltage regulator
