# Fritzing sketch sketch (saved by Fritzing 0.7.10b)
breadboards: 1

parts:
  Arduino1 = Arduino
  J1 = Basic Servo
  C1 = Electrolytic Capacitor [capacitance=100μF package="0807 [SMD, electrolytic]"]
  VCC1 = Battery block 9V

nets:
  N1: Arduino1.D9, J1.pulse
  +5V: Arduino1.+5V, J1.vcc, C1.+
  GND: Arduino1.GND, J1.gnd, C1.-, VCC1.-
  N2: Arduino1.VIN, VCC1.+
